# Fritzing sketch 1588BS-MAX7219CNG (saved by Fritzing 0.9.3b)
breadboards: 2

parts:
  Disp1 = LBT2088AH [part_number=LBT2088AH]
  Part1 = Arduino Uno (Rev3) - ICSP
  U1 = MAX7219 [package=dil24]
  R1 = Resistor [tolerance=±5% resistance=10k package="0805 [SMD]"]
  R2 = Resistor [tolerance=±5% resistance=10k package="0805 [SMD]"]
  R3 = Resistor [tolerance=±5% resistance=10k package="0805 [SMD]"]
  R4 = Resistor [tolerance=±5% resistance=10k package="0805 [SMD]"]

nets:
  N1: Disp1.pin1, U1.SEGD
  N2: Disp1.pin2, U1.SEGF
  N3: Disp1.pin_3, U1.DIG1
  N4: Disp1.pin_4, U1.DIG2
  N5: Disp1.pin_5, U1.SEGG
  N6: Disp1.pin_6, U1.DIG4
  N7: Disp1.pin_7, U1.SEGE
  N8: Disp1.pin_8, U1.SEGB
  N9: Disp1.pin_9, U1.SEGDP
  N10: Disp1.pin_10, U1.DIG3
  N11: Disp1.pin_11, U1.DIG5
  N12: Disp1.pin_12, U1.SEGC
  N13: Disp1.pin_13, U1.DIG0
  N14: Disp1.pin_14, U1.SEGA
  N15: Disp1.pin_15, U1.DIG6
  N16: Disp1.pin_16, U1.DIG7
  N17: Part1.D11_PWM/MOSI, U1.LOAD
  N18: Part1.D12/MISO, U1.CLK
  N19: Part1.D13/SCK, U1.DIN
  5V: Part1.5V, U1.VCC, R1.Pin_0
  GND: Part1.GND, U1.GND, U1.GND2
  N20: U1.ISET, R4.Pin_0
  N21: R1.Pin_1, R2.Pin_1
  N22: R2.Pin_0, R3.Pin_1
  N23: R3.Pin_0, R4.Pin_1
